# Fritzing sketch Wiring and schematic (saved by Fritzing 1.0.5)
circuit board: 8.46667cm x 5.64444cm

parts:
  ATTINY85 = attiny85 [package=dip]
  433mHz_Transmitter = RF-LINK_TX [package=rf-link_tx]
  JST_connector_-_1s_LiPo = Header 2 [package=jst-2-pth-kit]
  LED1 = LED - 5mm [color="Red (633nm)" current=0.030A package="5 mm [THT]"]
  R1 = Resistor [tolerance=±5% power=0.25W resistance=220 package=THT]

nets:
  N1: ATTINY85.Pin_4, 433mHz_Transmitter.GND, JST_connector_-_1s_LiPo.1, LED1.anode
  N2: ATTINY85.Pin_6, 433mHz_Transmitter.DATA, R1.Pin_0
  N3: ATTINY85.Pin_8, 433mHz_Transmitter.+5V, JST_connector_-_1s_LiPo.2
  N4: LED1.cathode, R1.Pin_1
